# Fritzing sketch schematic (saved by Fritzing 0.9.3b)
breadboards: 1

parts:
  part = Arduino Uno (Rev3) - ICSP
  part_2 = mini DIN 6 Connector [package=mini-din6]

nets:
  N1: part.5V, part_2.2
  N2: part.GND, part_2.6
  N3: part.D3_PWM, part_2.3
  N4: part.D5_PWM, part_2.5
