# Fritzing sketch simon_types_breadboard (saved by Fritzing 0.9.3b)
breadboards: 1

parts:
  LCD1 = LCD screen
  Part1 = Arduino Uno (Rev3) - ICSP
  R1 = Resistor [tolerance=±5% resistance=220 package=THT]
  R2 = Trimmer Potentiometer [maximum_resistance=10kΩ package=THT]
  R4 = Resistor [tolerance=±5% resistance=220 package=THT]
  R5 = Resistor [tolerance=±5% resistance=220 package=THT]
  LED2 = LED - 5mm [color="Green (555nm)" package="5 mm [THT]"]
  LED3 = LED - 5mm [color="Red (633nm)" package="5 mm [THT]"]
  U1 = mini DIN 6 Connector [package=mini-din6]

nets (from the breadboard view):
  VSS: LCD1.VSS, LCD1.R/W, LCD1.LED-, Part1.GND, R2.leg1, LED2.cathode, LED3.cathode, U1.4
  VDD: LCD1.VDD, LCD1.LED+, Part1.5V, R1.Pin_0, R1.Pin_1, R2.leg2, U1.5
  N1: LCD1.V0, R2.wiper
  N2: LCD1.RS, Part1.D12/MISO
  N3: LCD1.E, Part1.D11_PWM/MOSI
  N4: LCD1.DB4, Part1.D7
  N5: LCD1.DB5, Part1.D6_PWM
  N6: LCD1.DB6, Part1.D5_PWM
  N7: LCD1.DB7, Part1.D4
  N8: Part1.D8, U1.2
  N9: Part1.D9_PWM, R5.Pin_0, R5.Pin_1, LED3.anode
  N10: Part1.D10_PWM/SS, R4.Pin_0, R4.Pin_1, LED2.anode
  N11: Part1.D3_PWM, U1.3
