# Fritzing sketch simon_types_schematic (saved by Fritzing 0.9.3b)
breadboards: 1

parts:
  - = Arduino Uno (Rev3) - ICSP
  -_2 = LCD screen
  -_3 = Resistor [tolerance=±5% resistance=220 package=THT]
  -_4 = Trimmer Potentiometer [maximum_resistance=10kΩ package=THT]
  -_5 = LED - 5mm [color="Green (555nm)" package="5 mm [THT]"]
  -_6 = LED - 5mm [color="Red (633nm)" package="5 mm [THT]"]
  R1 = Resistor [tolerance=±5% resistance=220 package=THT]
  R2 = Resistor [tolerance=±5% resistance=220 package=THT]
  U1 = mini DIN 6 Connector [package=mini-din6]

nets:
  5V: -.5V, -_2.VDD, -_4.leg1, U1.4
  GND: -.GND, -_2.VSS, -_2.R/W, -_2.LED-, -_4.leg2, -_5.cathode, -_6.cathode, U1.5
  N1: -.D8, U1.2
  N2: -.D9_PWM, R1.Pin_0
  N3: -.D10_PWM/SS, R2.Pin_0
  N4: -.D11_PWM/MOSI, -_2.E
  N5: -.D12/MISO, -_2.RS
  N6: -.D2, U1.3
  N7: -.D3_PWM, -_2.DB7
  N8: -.D4, -_2.DB6
  N9: -.D5_PWM, -_2.DB5
  N10: -.D6_PWM, -_2.DB4
  N11: -_2.V0, -_4.wiper
  N12: -_2.LED+, -_3.Pin_1
  N13: -_5.anode, R1.Pin_1
  N14: -_6.anode, R2.Pin_1

notes:
  PS2 Connector
