# Fritzing sketch simon_types_v1_breadboard (saved by Fritzing 0.9.3b)
breadboards: 1

parts:
  LCD1 = LCD screen
  Part1 = Arduino Uno (Rev3) - ICSP
  R1 = Resistor [tolerance=±5% resistance=220 package=THT]
  R2 = Trimmer Potentiometer [maximum_resistance=10kΩ package=THT]
  LED1 = LED - 3mm [color="Red (633nm)" package="3 mm [THT]"]
  LED2 = LED - 3mm [color="Green (555nm)" package="3 mm [THT]"]
  R4 = Resistor [tolerance=±5% resistance=220 package=THT]
  R3 = Resistor [tolerance=±5% resistance=220 package=THT]  # not connected

nets:
  VSS: LCD1.VSS, LCD1.R/W, LCD1.LED-, Part1.GND, R2.leg1, LED1.cathode, LED2.cathode
  VDD: LCD1.VDD, LCD1.LED+, Part1.5V, R1.Pin_0, R1.Pin_1, R2.leg2
  N1: LCD1.V0, R2.wiper
  N2: LCD1.RS, Part1.D12/MISO
  N3: LCD1.E, Part1.D11_PWM/MOSI
  N4: LCD1.DB4, Part1.D6_PWM
  N5: LCD1.DB5, Part1.D5_PWM
  N6: LCD1.DB6, Part1.D4
  N7: LCD1.DB7, Part1.D3_PWM
  N8: Part1.D10_PWM/SS, R4.Pin_1

notes:
  PS2 Connector
  Data
  Clock
